// Logisim project led_image_loader.circ as structural Verilog: 15 circuits, main circuit main
module _4bit_adder_test (
  input  [3:0] a,
  input  [3:0] b,
  output [3:0] sum,
  output out_4
);

  _4bit_bus_full_adder u_4bit_bus_full_adder_1 (.a(a), .b(b), .sum(sum), .carry_in(1'b0), .carry_out(out_4));
endmodule

module _1bit_full_adder (
  input  input_0,
  input  input_1,
  input  carry_in,
  output sum,
  output carry_out
);

  wire and_1_out, and_2_out, and_3_out, and_4_out, and_5_out, and_6_out, and_7_out, and_8_out;

  and and_1 (and_1_out, ~input_0, ~input_1, carry_in);  // AND_Gate
  and and_2 (and_2_out, ~input_0, input_1, ~carry_in);  // AND_Gate
  and and_3 (and_3_out, input_0, ~input_1, ~carry_in);  // AND_Gate
  and and_4 (and_4_out, input_0, input_1, carry_in);
  and and_5 (and_5_out, ~input_0, input_1, carry_in);  // AND_Gate
  and and_6 (and_6_out, input_0, ~input_1, carry_in);  // AND_Gate
  and and_7 (and_7_out, input_0, input_1, ~carry_in);  // AND_Gate
  and and_8 (and_8_out, input_0, input_1, carry_in);
  or or_1 (sum, and_1_out, and_2_out, and_3_out, and_4_out);
  or or_2 (carry_out, and_5_out, and_6_out, and_7_out, and_8_out);
endmodule

module _4bit_full_adder (
  input  carry_in,
  input  a0,
  input  b0,
  input  a1,
  input  b1,
  input  a2,
  input  b2,
  input  a3,
  input  b3,
  output s0,
  output s1,
  output s2,
  output s3,
  output carry_out
);

  wire n1bit_full_adder_1_carry_out, n1bit_full_adder_2_carry_out, n1bit_full_adder_3_carry_out;

  _1bit_full_adder u_1bit_full_adder_1 (
    .sum(s0), .carry_out(n1bit_full_adder_1_carry_out), .input_0(a0), .input_1(b0), .carry_in(carry_in));
  _1bit_full_adder u_1bit_full_adder_2 (
    .sum(s1), .carry_out(n1bit_full_adder_2_carry_out), .input_0(a1), .input_1(b1),
    .carry_in(n1bit_full_adder_1_carry_out));
  _1bit_full_adder u_1bit_full_adder_3 (
    .sum(s2), .carry_out(n1bit_full_adder_3_carry_out), .input_0(a2), .input_1(b2),
    .carry_in(n1bit_full_adder_2_carry_out));
  _1bit_full_adder u_1bit_full_adder_4 (
    .sum(s3), .carry_out(carry_out), .input_0(a3), .input_1(b3), .carry_in(n1bit_full_adder_3_carry_out));
endmodule

module _4bit_bus_full_adder (
  input  carry_in,
  input  [3:0] a,
  input  [3:0] b,
  output [3:0] sum,
  output carry_out
);

  _4bit_full_adder u_4bit_full_adder_1 (
    .a0(a[0]), .b0(b[0]), .a1(a[1]), .b1(b[1]), .a2(a[2]), .b2(b[2]), .a3(a[3]), .b3(b[3]), .s0(sum[0]),
    .s1(sum[1]), .s2(sum[2]), .s3(sum[3]), .carry_in(carry_in), .carry_out(carry_out));
endmodule

module SR_Latch (
  input  R,
  input  S,
  input  CLR,
  output Q,
  output nQ
);

  wire nor_1_out, nor_2_out;

  nor nor_1 (nor_1_out, R, nor_2_out);
  nor nor_2 (nor_2_out, Q, S);
  and and_1 (Q, nor_1_out, ~CLR);  // AND_Gate
  or or_1 (nQ, nor_2_out, CLR);
endmodule

module D_Latch (
  input  CLK,
  input  D,
  input  CLR,
  output Q,
  output nQ
);

  wire and_1_out, and_2_out;

  and and_1 (and_1_out, CLK, ~D);  // AND_Gate
  and and_2 (and_2_out, CLK, D);
  SR_Latch sr_latch_1 (.R(and_1_out), .S(and_2_out), .Q(Q), .nQ(nQ), .CLR(CLR));
endmodule

module D_Flip_Flop (
  input  CLK,
  input  D,
  input  CLR,
  output out_4
);

  wire d_latch_1_q, not_1_out;

  not not_1 (not_1_out, CLK);
  D_Latch d_latch_1 (.CLK(not_1_out), .D(D), .CLR(CLR), .Q(d_latch_1_q));  // open: nQ
  D_Latch d_latch_2 (.CLK(CLK), .D(d_latch_1_q), .CLR(CLR), .Q(out_4));  // open: nQ
endmodule

module _4bit_register (
  input  CLK,
  input  D0,
  input  D1,
  input  D2,
  input  D3,
  input  CLR,
  output Q0,
  output Q1,
  output Q2,
  output Q3
);

  D_Flip_Flop d_flip_flop_1 (.CLK(CLK), .D(D0), .CLR(CLR), .out_4(Q0));
  D_Flip_Flop d_flip_flop_2 (.CLK(CLK), .D(D1), .CLR(CLR), .out_4(Q1));
  D_Flip_Flop d_flip_flop_3 (.CLK(CLK), .D(D2), .CLR(CLR), .out_4(Q2));
  D_Flip_Flop d_flip_flop_4 (.CLK(CLK), .D(D3), .CLR(CLR), .out_4(Q3));
endmodule

module _4_bit_counter_test (
  input  CLR,
  output [3:0] out_2
);

  wire clock_1_out;
  wire [3:0] n4bit_bus_full_adder_1_sum;

  Clock clock_1 (.out(clock_1_out));
  _4bit_register u_4bit_register_1 (
    .CLK(clock_1_out), .D0(n4bit_bus_full_adder_1_sum[0]), .D1(n4bit_bus_full_adder_1_sum[1]),
    .D2(n4bit_bus_full_adder_1_sum[2]), .D3(n4bit_bus_full_adder_1_sum[3]), .CLR(CLR), .Q0(out_2[0]),
    .Q1(out_2[1]), .Q2(out_2[2]), .Q3(out_2[3]));
  _4bit_bus_full_adder u_4bit_bus_full_adder_1 (
    .a(out_2), .b(4'b0001), .sum(n4bit_bus_full_adder_1_sum), .carry_in(1'b0));  // open: carry_out
  Hex_Digit_Display hex_digit_display_1 (.value(out_2));  // open: dp
endmodule

module _8bit_bus_register (
  input  CLK,
  input  [7:0] in,
  input  CLR,
  output [7:0] out
);

  _4bit_register u_4bit_register_1 (
    .CLK(CLK), .D0(in[0]), .D1(in[1]), .D2(in[2]), .D3(in[3]), .CLR(CLR), .Q0(out[0]), .Q1(out[1]),
    .Q2(out[2]), .Q3(out[3]));
  _4bit_register u_4bit_register_2 (
    .CLK(CLK), .D0(in[4]), .D1(in[5]), .D2(in[6]), .D3(in[7]), .CLR(CLR), .Q0(out[4]), .Q1(out[5]),
    .Q2(out[6]), .Q3(out[7]));
endmodule

module _8_byte_register_file (
  input  [7:0] WD,
  input  CLK,
  input  WE,
  input  [2:0] WA,
  input  CLR,
  output [7:0] out0,
  output [7:0] out1,
  output [7:0] out2,
  output [7:0] out3,
  output [7:0] out4,
  output [7:0] out5,
  output [7:0] out6,
  output [7:0] out7
);

  wire and_1_out, and_2_out, and_3_out, and_4_out, and_5_out, and_6_out, and_7_out, and_8_out, and_9_out,
       n8bit_decoder_1_out0, n8bit_decoder_1_out1, n8bit_decoder_1_out2, n8bit_decoder_1_out3,
       n8bit_decoder_1_out4, n8bit_decoder_1_out5, n8bit_decoder_1_out6, n8bit_decoder_1_out7;

  and and_1 (and_1_out, CLK, WE);
  _8bit_decoder u_8bit_decoder_1 (
    .select(WA), .out0(n8bit_decoder_1_out0), .out7(n8bit_decoder_1_out7), .out1(n8bit_decoder_1_out1),
    .out6(n8bit_decoder_1_out6), .out2(n8bit_decoder_1_out2), .out3(n8bit_decoder_1_out3),
    .out4(n8bit_decoder_1_out4), .out5(n8bit_decoder_1_out5));
  and and_2 (and_2_out, and_1_out, n8bit_decoder_1_out0);
  and and_3 (and_3_out, and_1_out, n8bit_decoder_1_out2);
  and and_4 (and_4_out, and_1_out, n8bit_decoder_1_out4);
  and and_5 (and_5_out, and_1_out, n8bit_decoder_1_out6);
  _8bit_bus_register u_8bit_bus_register_1 (.CLK(and_2_out), .in(WD), .CLR(CLR), .out(out0));
  _8bit_bus_register u_8bit_bus_register_2 (.CLK(and_3_out), .in(WD), .CLR(CLR), .out(out2));
  _8bit_bus_register u_8bit_bus_register_3 (.CLK(and_4_out), .in(WD), .CLR(CLR), .out(out4));
  _8bit_bus_register u_8bit_bus_register_4 (.CLK(and_5_out), .in(WD), .CLR(CLR), .out(out6));
  and and_6 (and_6_out, and_1_out, n8bit_decoder_1_out1);
  and and_7 (and_7_out, and_1_out, n8bit_decoder_1_out3);
  and and_8 (and_8_out, and_1_out, n8bit_decoder_1_out5);
  and and_9 (and_9_out, and_1_out, n8bit_decoder_1_out7);
  _8bit_bus_register u_8bit_bus_register_5 (.CLK(and_6_out), .in(WD), .CLR(CLR), .out(out1));
  _8bit_bus_register u_8bit_bus_register_6 (.CLK(and_7_out), .in(WD), .CLR(CLR), .out(out3));
  _8bit_bus_register u_8bit_bus_register_7 (.CLK(and_8_out), .in(WD), .CLR(CLR), .out(out5));
  _8bit_bus_register u_8bit_bus_register_8 (.CLK(and_9_out), .in(WD), .CLR(CLR), .out(out7));
endmodule

module _8bit_decoder (
  input  [2:0] select,
  output out0,
  output out1,
  output out2,
  output out3,
  output out4,
  output out5,
  output out6,
  output out7
);

  and and_1 (out0, ~select[2], ~select[1], ~select[0]);  // AND_Gate
  and and_2 (out1, ~select[2], ~select[1], select[0]);  // AND_Gate
  and and_3 (out2, ~select[2], select[1], ~select[0]);  // AND_Gate
  and and_4 (out3, ~select[2], select[1], select[0]);  // AND_Gate
  and and_5 (out4, select[2], ~select[1], ~select[0]);  // AND_Gate
  and and_6 (out5, select[2], ~select[1], select[0]);  // AND_Gate
  and and_7 (out6, select[2], select[1], ~select[0]);  // AND_Gate
  and and_8 (out7, select[2], select[1], select[0]);
endmodule

module main (
  input  CLR,
  output [7:0] out_2,
  output [7:0] out_3,
  output [7:0] out_4,
  output [7:0] out_5,
  output [7:0] out_6,
  output [7:0] out_7,
  output [7:0] out_8,
  output [7:0] out_9,
  output [7:0] out_10
);

  wire CLK_out, not_1_out;
  wire [3:0] n4_bit_counter_1_out_6;

  Clock CLK (.out(CLK_out));
  not not_1 (not_1_out, CLK_out);
  _4_bit_counter u_4_bit_counter_1 (
    .CLR(CLR), .out_3(n4_bit_counter_1_out_6[0]), .out_4(n4_bit_counter_1_out_6[1]),
    .out_5(n4_bit_counter_1_out_6[2]), .out_6(n4_bit_counter_1_out_6[3]), .CLK(not_1_out));
  ROM #(.addrWidth(4)) rom_1 (.addr(n4_bit_counter_1_out_6), .data(out_2));  // open: sel
  _8_byte_register_file u_8_byte_register_file_1 (
    .WD(out_2), .CLK(CLK_out), .WE(1'b1), .WA(n4_bit_counter_1_out_6[2:0]), .CLR(CLR), .out0(out_3),
    .out1(out_4), .out2(out_5), .out3(out_6), .out4(out_7), .out5(out_8), .out6(out_9), .out7(out_10));
  DotMatrix #(.inputtype("row"), .matrixcols(8), .matrixrows(8)) dotmatrix_1 (
    .row0(out_3), .row1(out_4), .row2(out_5), .row3(out_6), .row4(out_7), .row5(out_8), .row6(out_9),
    .row7(out_10));

  // Notes on the sheet:
  //   contents of rom_1 (hex, n*v repeats v):
  //   80 40 20 10 8 4 2 1 1 2 4 8 10 20 40 80
endmodule

module _4_bit_counter (
  input  CLK,
  input  CLR,
  output out_3,
  output out_4,
  output out_5,
  output out_6
);

  wire n4bit_full_adder_1_s0, n4bit_full_adder_1_s1, n4bit_full_adder_1_s2, n4bit_full_adder_1_s3;

  _4bit_register u_4bit_register_1 (
    .CLK(CLK), .D0(n4bit_full_adder_1_s0), .D1(n4bit_full_adder_1_s1), .D2(n4bit_full_adder_1_s2),
    .D3(n4bit_full_adder_1_s3), .CLR(CLR), .Q0(out_3), .Q1(out_4), .Q2(out_5), .Q3(out_6));
  _4bit_full_adder u_4bit_full_adder_1 (
    .a0(1'b1), .b0(out_3), .a1(1'b0), .b1(out_4), .a2(1'b0), .b2(out_5), .a3(1'b0), .b3(out_6),
    .s0(n4bit_full_adder_1_s0), .s1(n4bit_full_adder_1_s1), .s2(n4bit_full_adder_1_s2),
    .s3(n4bit_full_adder_1_s3), .carry_in(1'b0));  // open: carry_out
endmodule

module _4_bit_D_flip_flop (
  input  CLR,
  input  CLK,
  input  in0,
  input  in1,
  input  in2,
  input  in3,
  output out0,
  output out1,
  output out2,
  output out3
);

  D_Flip_Flop d_flip_flop_1 (.CLK(CLK), .D(in0), .CLR(CLR), .out_4(out0));
  D_Flip_Flop d_flip_flop_2 (.CLK(CLK), .D(in1), .CLR(CLR), .out_4(out1));
  D_Flip_Flop d_flip_flop_3 (.CLK(CLK), .D(in2), .CLR(CLR), .out_4(out2));
  D_Flip_Flop d_flip_flop_4 (.CLK(CLK), .D(in3), .CLR(CLR), .out_4(out3));
endmodule
